// Logisim project tx_base_baud_shift.circ as structural Verilog: 2 circuits, main circuit baud_rate
module baud_rate (
);

  wire clock_1_out;
  wire [3:0] counter_1_q;

  Clock clock_1 (.out(clock_1_out));
  Counter #(.max('hf), .width(4)) counter_1 (
    .clk(clock_1_out), .Q(counter_1_q));  // open: clr, load, up, count, D, carry
  LED led_1 (.in(counter_1_q[0]));
  LED led_2 (.in(counter_1_q[1]));
  LED led_3 (.in(counter_1_q[2]));
  LED led_4 (.in(counter_1_q[3]));
endmodule

module shift_165 (
  input  b4,
  input  b5,
  input  b6,
  input  b7,
  input  in_5,
  input  b3,
  input  b2,
  input  b1,
  input  b0
);

  wire n74165_1_pin2, n74165_1_pin9, n74165_1_pin10, n74165_1_pin15;

  _74165 u_74165_1 (
    .pin1(in_5), .pin2(n74165_1_pin2), .pin3(b3), .pin4(b2), .pin5(b1), .pin6(b0), .pin15(n74165_1_pin15),
    .pin14(b4), .pin13(b5), .pin12(b6), .pin11(b7), .pin10(n74165_1_pin10), .pin9(n74165_1_pin9));  // open: pin7
  Clock clock_1 (.out(n74165_1_pin2));
  LED led_1 (.in(n74165_1_pin9));
  // also tied to GND on the sheet: n74165_1_pin15
  // also tied to VCC on the sheet: n74165_1_pin10
endmodule
