// Logisim project tx_frame_controller.circ as structural Verilog: 1 circuit, main circuit main
module main (
  input  D6,
  input  D5,
  input  D4,
  input  D3,
  input  D2,
  input  D1,
  input  D0,
  input  SEND,
  input  RESET,
  input  D7
);

  wire n7408_1_pin3, n7408_1_pin4, n7408_1_pin5, n7408_1_pin6, n7408_1_pin9, n7408_1_pin10, n7432_1_pin6,
       n7474_1_pin2, n7474_1_pin4, n7474_1_pin8, n74161_1_pin3, n74161_1_pin7, n74161_1_pin12,
       n74161_1_pin14, TB1, TBCLK1, TNBUSY1, TQH1, U1_pin6, U1_pin10, U1_pin15, U2_pin3, U2_pin5, U2_pin14,
       U2_pin15, X1_pin3, X1_pin6, X1_pin8, X1_pin11, X2_pin3, X2_pin6;

  Clock BCLK (.out(TBCLK1));
  _7474 u_7474_1 (
    .pin1(RESET), .pin2(n7474_1_pin2), .pin3(TBCLK1), .pin4(n7474_1_pin4), .pin5(TB1), .pin13(n7474_1_pin4),
    .pin12(SEND), .pin11(TBCLK1), .pin10(n7474_1_pin4), .pin8(n7474_1_pin8));  // open: pin6, pin9
  LED NBUSY (.in(TNBUSY1));
  LED TX (.in(n7432_1_pin6));
  LED BUSY (.in(TB1));
  _7408 u_7408_1 (
    .pin1(SEND), .pin2(n7474_1_pin8), .pin3(n7408_1_pin3), .pin4(n7408_1_pin4), .pin5(n7408_1_pin5),
    .pin6(n7408_1_pin6), .pin10(n7408_1_pin10), .pin9(n7408_1_pin9), .pin8(n7474_1_pin2));  // open: pin13, pin12, pin11
  _7432 u_7432_1 (
    .pin1(n7408_1_pin3), .pin2(TB1), .pin3(n7408_1_pin9), .pin4(TQH1), .pin5(TNBUSY1), .pin6(n7432_1_pin6));  // open: pin13, pin12, pin11, pin10, pin9, pin8
  _7404 u_7404_1 (
    .pin1(n7408_1_pin6), .pin2(n7408_1_pin10), .pin3(TB1), .pin4(TNBUSY1));  // open: pin5, pin6, pin13, pin12, pin11, pin10, pin9, pin8
  LED NDONE (.in(n7408_1_pin10));
  _74161 u_74161_1 (
    .pin1(TB1), .pin2(TBCLK1), .pin3(n74161_1_pin3), .pin4(n74161_1_pin3), .pin5(n74161_1_pin3),
    .pin6(n74161_1_pin3), .pin7(n74161_1_pin7), .pin14(n74161_1_pin14), .pin13(n7408_1_pin5),
    .pin12(n74161_1_pin12), .pin11(n7408_1_pin4), .pin10(n74161_1_pin7), .pin9(n74161_1_pin7));  // open: pin15
  LED START (.in(n7408_1_pin3));
  LED QB (.in(n7408_1_pin5));
  LED QD (.in(n7408_1_pin4));
  LED QA (.in(n74161_1_pin14));
  LED QC (.in(n74161_1_pin12));
  LED DONE (.in(n7408_1_pin6));
  _7486 X1 (
    .pin1(D0), .pin2(D1), .pin3(X1_pin3), .pin4(D2), .pin5(D3), .pin6(X1_pin6), .pin13(D7), .pin12(D6),
    .pin11(X1_pin11), .pin10(D5), .pin9(D4), .pin8(X1_pin8));
  _74165 U1 (
    .pin1(TB1), .pin2(TBCLK1), .pin3(D2), .pin4(D1), .pin5(D0), .pin6(U1_pin6), .pin15(U1_pin15), .pin14(D3),
    .pin13(D4), .pin12(D5), .pin11(D6), .pin10(U1_pin10), .pin9(TQH1));  // open: pin7
  _74165 U2 (
    .pin1(TB1), .pin2(TBCLK1), .pin3(U2_pin3), .pin4(U2_pin3), .pin5(U2_pin5), .pin6(D7), .pin15(U2_pin15),
    .pin14(U2_pin14), .pin13(U2_pin14), .pin12(U2_pin14), .pin11(U2_pin14), .pin10(U2_pin14), .pin9(U1_pin10));  // open: pin7
  LED X6_7 (.in(X1_pin11));
  LED X0_1 (.in(X1_pin3));
  LED X4_5 (.in(X1_pin8));
  LED X2_3 (.in(X1_pin6));
  LED QH1 (.in(TQH1));
  _7486 X2 (
    .pin1(X1_pin3), .pin2(X1_pin6), .pin3(X2_pin3), .pin4(X1_pin8), .pin5(X1_pin11), .pin6(X2_pin6),
    .pin10(X2_pin6), .pin9(X2_pin3), .pin8(U2_pin5));  // open: pin13, pin12, pin11
  LED X0a3 (.in(X2_pin3));
  LED X4a7 (.in(X2_pin6));
  LED P (.in(U2_pin5));
  // also tied to GND on the sheet: {n74161_1_pin3, U1_pin15, U2_pin15, U1_pin6}
  // also tied to VCC on the sheet: {n7474_1_pin4, n74161_1_pin7, U2_pin14, U2_pin3}

  // Other names for the same wires on the sheet: TBCLK2 = TBCLK1; TD0 = D0; TD1 = D1; TD2 = D2; TD3 = D3; TD4 = D4;
  //   TD5 = D5; TD6 = D6; TD7 = D7
endmodule
